# Fritzing sketch schema (saved by Fritzing 0.9.0b)
breadboards: 1

parts:
  Onderdeel1 = Arduino Uno (Rev3)
  LED1 = LED - 5mm [color="Red (633nm)" package="5 mm [THT]"]
  J1 = Basic Servo
  S1 = Pushbutton [package="[SMD]"]
  U1 = POT [package=pot_mammoth]
  R1 = Resistor [tolerance=±5% resistance=10k package=THT]

nets:
  N1: Onderdeel1.A0, U1.A
  N2: Onderdeel1.D8, S1.Pin_1, S1.Pin_2, R1.Pin_1
  N3: Onderdeel1.D10_PWM/SS, J1.pulse
  N4: Onderdeel1.D13/SCK, LED1.anode
  5V: Onderdeel1.5V, J1.vcc, S1.Pin_3, S1.Pin_4, U1.E
  GND: Onderdeel1.GND, LED1.cathode, J1.gnd, U1.S, R1.Pin_0
